// Digital circuit cpu.dig as structural Verilog
module cpu (
  input  Clk,
  input  [15:0] MemIn,
  input  MemReady,
  output [15:0] MemAddr,
  output [15:0] MemOut
);

  wire [15:0] register_1_q;

  Register #(.Bits(16)) register_1 (.D(MemIn), .C(Clk), .en(MemReady), .Q(register_1_q));
endmodule
